// Logisim project real_Alu.circ as structural Verilog: 19 circuits, main circuit in_A and in_B
module in_A_and_in_B (
  input  [7:0] in_1,
  input  [7:0] in_2,
  output [7:0] out_3
);

  assign out_3 = in_1 & in_2;  // AND_Gate and_1, 8 bits wide
endmodule

module in_A_or_in_B (
  input  [7:0] in_1,
  input  [7:0] in_2,
  output [7:0] out_3
);

  assign out_3 = in_1 | in_2;  // OR_Gate or_1, 8 bits wide
endmodule

module not_in_B (
  input  [7:0] in_1,
  output [7:0] out_2
);

  assign out_2 = ~in_1;  // NOT_Gate not_1, 8 bits wide
endmodule

module LSL_in_b (
  input  [7:0] Num_b,
  output out_2,
  output [7:0] out_3
);


  assign out_2 = Num_b[7];
  assign out_3 = {Num_b[6:0], 1'b0};
endmodule

module LSR_in_b (
  input  [7:0] Num_b,
  output out_2,
  output [7:0] out_3
);


  assign out_2 = Num_b[0];
  assign out_3 = {1'b0, Num_b[7:1]};
endmodule

module in_A_add_in_B (
  input  [7:0] in_1,
  input  [7:0] in_2,
  output [7:0] out_3,
  output out_4
);

  odio_puro odio_puro_1 (.in_1(in_1), .in_2(in_2), .out_3(out_3), .out_4(out_4));
endmodule

module half_adder (
  input  a,
  input  b,
  output S,
  output c
);

  xor xor_1 (S, a, b);
  and and_1 (c, a, b);
endmodule

module full_adder (
  input  C0,
  input  a,
  input  b,
  output S,
  output c
);

  wire and_1_out, and_2_out, and_3_out, xor_1_out;

  xor xor_1 (xor_1_out, a, b);
  and and_1 (and_1_out, C0, a);
  and and_2 (and_2_out, C0, b);
  and and_3 (and_3_out, a, b);
  xor xor_2 (S, xor_1_out, C0);
  or or_1 (c, and_1_out, and_2_out, and_3_out);
endmodule

module adder1 (
  input  a1,
  input  a2,
  input  a3,
  input  a0,
  input  b1,
  input  b2,
  input  b3,
  input  b0,
  input  in_9,
  output O0,
  output O1,
  output O2,
  output out_13,
  output out_14
);

  wire full_adder_1_c, full_adder_2_c, full_adder_3_c;

  full_adder full_adder_1 (.S(O0), .c(full_adder_1_c), .C0(in_9), .a(a0), .b(b0));
  full_adder full_adder_2 (.S(O1), .c(full_adder_2_c), .C0(full_adder_1_c), .a(a1), .b(b1));
  full_adder full_adder_3 (.S(O2), .c(full_adder_3_c), .C0(full_adder_2_c), .a(a2), .b(b2));
  full_adder full_adder_4 (.S(out_13), .c(out_14), .C0(full_adder_3_c), .a(a3), .b(b3));
endmodule

module _8_bitter_adder (
  input  a3,
  input  a2,
  input  a1,
  input  a0,
  input  b3,
  input  b2,
  input  b1,
  input  b0,
  input  a7,
  input  a6,
  input  a5,
  input  a4,
  input  b7,
  input  b6,
  input  b5,
  input  b4,
  output [3:0] out_17,
  output [3:0] out_18,
  output out_19
);

  wire adder1_1_out_14;

  adder1 adder1_1 (
    .a1(a1), .a2(a2), .a3(a3), .a0(a0), .b1(b1), .b2(b2), .b3(b3), .b0(b0), .out_14(adder1_1_out_14),
    .O0(out_17[0]), .O1(out_17[1]), .O2(out_17[2]), .out_13(out_17[3]), .in_9(1'b0));
  adder1 adder1_2 (
    .a1(a5), .a2(a6), .a3(a7), .a0(a4), .b1(b5), .b2(b6), .b3(b7), .b0(b4), .out_14(out_19), .O0(out_18[0]),
    .O1(out_18[1]), .O2(out_18[2]), .out_13(out_18[3]), .in_9(adder1_1_out_14));
endmodule

module odio_puro (
  input  [7:0] in_1,
  input  [7:0] in_2,
  output [7:0] out_3,
  output out_4
);

  _8_bitter_adder u_8_bitter_adder_1 (
    .a3(in_1[3]), .a2(in_1[2]), .a1(in_1[1]), .a0(in_1[0]), .b3(in_2[3]), .b2(in_2[2]), .b1(in_2[1]),
    .b0(in_2[0]), .a7(in_1[7]), .a6(in_1[6]), .a5(in_1[5]), .a4(in_1[4]), .b7(in_2[7]), .b6(in_2[6]),
    .b5(in_2[5]), .b4(in_2[4]), .out_17(out_3[3:0]), .out_18(out_3[7:4]), .out_19(out_4));
endmodule

module in_A_sub_in_B (
  input  [7:0] in_1,
  input  [7:0] in_2,
  output [7:0] out_3,
  output out_4
);

  wire [7:0] complemento_a_due_1_out_2;

  complemento_a_due complemento_a_due_1 (.in_1(in_2), .out_2(complemento_a_due_1_out_2));
  odio_puro odio_puro_1 (.in_1(in_1), .in_2(complemento_a_due_1_out_2), .out_3(out_3), .out_4(out_4));
endmodule

module complemento_a_due (
  input  [7:0] in_1,
  output [7:0] out_2
);

  wire half_adder_1_c, half_adder_2_c, half_adder_3_c, half_adder_4_c, half_adder_5_c, half_adder_6_c,
       half_adder_7_c, half_adder_8_c;
  wire [7:0] not_1_out;

  assign not_1_out = ~in_1;  // NOT_Gate not_1, 8 bits wide
  half_adder half_adder_1 (.S(out_2[2]), .c(half_adder_1_c), .a(half_adder_2_c), .b(not_1_out[2]));
  half_adder half_adder_2 (.S(out_2[1]), .c(half_adder_2_c), .a(half_adder_3_c), .b(not_1_out[1]));
  half_adder half_adder_3 (.S(out_2[0]), .c(half_adder_3_c), .a(not_1_out[0]), .b(1'b1));
  half_adder half_adder_4 (.S(out_2[5]), .c(half_adder_4_c), .a(half_adder_5_c), .b(not_1_out[5]));
  half_adder half_adder_5 (.S(out_2[4]), .c(half_adder_5_c), .a(half_adder_6_c), .b(not_1_out[4]));
  half_adder half_adder_6 (.S(out_2[3]), .c(half_adder_6_c), .a(half_adder_1_c), .b(not_1_out[3]));
  LED led_1 (.in(half_adder_7_c));
  half_adder half_adder_7 (.S(out_2[7]), .c(half_adder_7_c), .a(half_adder_8_c), .b(not_1_out[7]));
  half_adder half_adder_8 (.S(out_2[6]), .c(half_adder_8_c), .a(half_adder_4_c), .b(not_1_out[6]));
endmodule

module inc_in_B (
  input  [7:0] in_1,
  output [7:0] out_2,
  output out_3
);

  in_A_add_in_B in_a_add_in_b_1 (.in_1(in_1), .in_2(8'h1), .out_3(out_2), .out_4(out_3));
endmodule

module dec_in_B (
  input  [7:0] in_1,
  output [7:0] out_2,
  output out_3
);

  in_A_sub_in_B in_a_sub_in_b_1 (.in_1(in_1), .in_2(8'h1), .out_3(out_2), .out_4(out_3));
endmodule

module mux (
  input  [7:0] in_1,
  input  [7:0] in_2,
  input  [3:0] in_3,
  output [7:0] out_4,
  output out_5,
  output N,
  output out_7,
  output out_8
);

  wire C, C1, or_1_out, V, V1;
  wire [7:0] dec_in_b_1_out_2, in_a_add_in_b_1_out_3, in_a_and_in_b_1_out_3, in_a_or_in_b_1_out_3,
       in_a_sub_in_b_1_out_3, inc_in_b_1_out_2, lsl_in_b_1_out_3, lsr_in_b_1_out_3, not_in_b_1_out_2;

  not_in_B not_in_b_1 (.in_1(in_2), .out_2(not_in_b_1_out_2));
  LSL_in_b lsl_in_b_1 (.Num_b(in_2), .out_2(V1), .out_3(lsl_in_b_1_out_3));
  LSR_in_b lsr_in_b_1 (.Num_b(in_2), .out_2(C1), .out_3(lsr_in_b_1_out_3));
  in_A_and_in_B in_a_and_in_b_1 (.in_1(in_1), .in_2(in_2), .out_3(in_a_and_in_b_1_out_3));
  in_A_or_in_B in_a_or_in_b_1 (.in_1(in_1), .in_2(in_2), .out_3(in_a_or_in_b_1_out_3));
  in_A_add_in_B in_a_add_in_b_1 (.in_1(in_1), .in_2(in_2), .out_3(in_a_add_in_b_1_out_3), .out_4(V));
  in_A_sub_in_B in_a_sub_in_b_1 (.in_1(in_1), .in_2(in_2), .out_3(in_a_sub_in_b_1_out_3), .out_4(C));
  inc_in_B inc_in_b_1 (.in_1(in_2), .out_2(inc_in_b_1_out_2));  // open: out_3
  dec_in_B dec_in_b_1 (.in_1(in_2), .out_2(dec_in_b_1_out_2));  // open: out_3
  Multiplexer #(.select(4)) multiplexer_1 (
    .in0(1'b0), .in1(1'b0), .in2(1'b0), .in3(1'b0), .in4(1'b0), .in5(V), .in6(V), .in7(V), .in8(V),
    .in9(1'b0), .in10(1'b0), .in11(1'b0), .in12(1'b0), .in13(1'b0), .in14(1'b0), .in15(1'b0), .out(out_7),
    .sel(in_3));  // open: en
  Multiplexer #(.select(4), .width(8)) multiplexer_2 (
    .in0(in_a_and_in_b_1_out_3), .in1(in_a_or_in_b_1_out_3), .in2(not_in_b_1_out_2), .in3(lsl_in_b_1_out_3),
    .in4(lsr_in_b_1_out_3), .in5(in_a_add_in_b_1_out_3), .in6(in_a_sub_in_b_1_out_3), .in7(inc_in_b_1_out_2),
    .in8(dec_in_b_1_out_2), .in9(in_1), .in10({8{1'b0}}), .in11({8{1'b0}}), .in12({8{1'b0}}),
    .in13({8{1'b0}}), .in14({8{1'b0}}), .in15({8{1'b0}}), .out(out_4), .sel(in_3));  // open: en
  or or_1 (or_1_out, C, C1, V1);
  z z_1 (.in_1(out_4), .out_2(out_5));
  n n_1 (.in_1(out_4), .in_2(in_3), .out_3(N));
  Multiplexer #(.select(4)) multiplexer_3 (
    .in0(1'b0), .in1(1'b0), .in2(1'b0), .in3(or_1_out), .in4(or_1_out), .in5(or_1_out), .in6(or_1_out),
    .in7(or_1_out), .in8(or_1_out), .in9(1'b0), .in10(1'b0), .in11(1'b0), .in12(1'b0), .in13(1'b0),
    .in14(1'b0), .in15(1'b0), .out(out_8), .sel(in_3));  // open: en

  // Other names for the same wires on the sheet: in_A[7:0] = in_1; in_B[7:0] = in_2; S[3:0] = in_3
endmodule

module z (
  input  [7:0] in_1,
  output out_2
);

  nor nor_1 (out_2, in_1[0], in_1[1], in_1[2], in_1[3], in_1[4], in_1[5], in_1[6], in_1[7]);
endmodule

module n (
  input  [7:0] in_1,
  input  [3:0] in_2,
  output out_3
);

  wire xnor_1_out;

  xnor xnor_1 (xnor_1_out, in_1[7], 1'b0);
  Multiplexer #(.select(4)) multiplexer_1 (
    .in0(1'b0), .in1(1'b0), .in2(1'b0), .in3(xnor_1_out), .in4(xnor_1_out), .in5(xnor_1_out),
    .in6(xnor_1_out), .in7(xnor_1_out), .in8(xnor_1_out), .in9(xnor_1_out), .in10(xnor_1_out),
    .in11(xnor_1_out), .in12(xnor_1_out), .in13(xnor_1_out), .in14(xnor_1_out), .in15(xnor_1_out),
    .out(out_3), .sel(in_2));  // open: en

  assign in_1[5:0] = {6{in_1[6]}};
  // also tied to GND on the sheet: in_1[6]
endmodule

module real_Alu (
  input  [7:0] in_1,
  input  [7:0] in_2,
  input  [3:0] in_3,
  output [7:0] out_4
);

  wire mux_1_n, mux_1_out_5, mux_1_out_7, mux_1_out_8;

  LED led_1 (.in(mux_1_out_8));
  LED led_2 (.in(mux_1_out_7));
  LED led_3 (.in(mux_1_n));
  mux mux_1 (
    .in_1(in_1), .in_2(in_2), .out_4(out_4), .N(mux_1_n), .in_3(in_3), .out_5(mux_1_out_5),
    .out_7(mux_1_out_7), .out_8(mux_1_out_8));
  LED led_4 (.in(mux_1_out_5));
endmodule
